# Fritzing sketch AV_Relay_Thermostat (saved by Fritzing 0.9.6b)
breadboards: 1

parts:
  OLED1 = OLED 128x64 I2C Monochrome Display VDD-GND
  Composant1 = Arduino Nano (Rev3.0)
  R1 = Temperature Sensor (Thermistor) [thermistor_type=NTC package=THT]
  R2 = Temperature Sensor (Thermistor) [thermistor_type=NTC package=THT]
  R3 = Resistor [tolerance=±5% resistance=10k package="1206 [SMD]"]
  S1 = Pushbutton [package="[SMD]"]
  S2 = Pushbutton [package="[SMD]"]
  S3 = Pushbutton [package="[SMD]"]
  R4 = Resistor [tolerance=±5% resistance=10k package="1206 [SMD]"]
  R7 = Resistor [tolerance=±5% resistance=1k package="1206 [SMD]"]
  R8 = Resistor [tolerance=±5% resistance=1k package="1206 [SMD]"]
  R5 = Resistor [tolerance=±5% resistance=10k package="1206 [SMD]"]
  R6 = Resistor [tolerance=±5% resistance=1k package="1206 [SMD]"]
  U3 = 2-Channel 5v Relay Shield [package=relay-2ch5v10a]

nets:
  VDD: OLED1.VDD, Composant1.AREF, Composant1.3V3, R3.Pin_1, R4.Pin_1
  GND: OLED1.GND, Composant1.GND, R1.pin_1, R2.pin_1, S1.Pin_3, S1.Pin_4, S2.Pin_3, S2.Pin_4, S3.Pin_3, S3.Pin_4, U3.GND
  N1: OLED1.SCK, Composant1.A5
  N2: OLED1.SDA, Composant1.A4
  N3: Composant1.D5, U3.IN1
  N4: Composant1.D6, U3.IN2
  5V: Composant1.5V, R5.Pin_1, U3.VCC
  N5: Composant1.A6, R5.Pin_0, R6.Pin_1
  N6: Composant1.A3, R1.pin_0, R3.Pin_0
  N7: Composant1.A2, R2.pin_0, R4.Pin_0
  N8: S1.Pin_1, S1.Pin_2, R8.Pin_0
  N9: S2.Pin_1, S2.Pin_2, R7.Pin_0, R8.Pin_1
  N10: S3.Pin_1, S3.Pin_2, R7.Pin_1, R6.Pin_0

custom parts:
  OLED 128x64 I2C Monochrome Display VDD-GND: OLED 128x64 I2C Monochrome Display. Note: there are two variants of this part, this one is the VDD GND SCK SDA variant. The other is GND VDD SCK SDA. Make sure you select the part that matches your module as using the incorrect part will probably destroy your module! In addition the mounting holes are marked on silkscreen but not by default drilled. If you want drilled mounting holes, copy a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
  2-Channel 5v Relay Shield: 2 Channel 5v Relay Shield w. 2x SPD-06VDC-SD-C

// code stored in the sketch: AV_Relay_Thermostat.ino
//__________________________________________________________________________________
// Relay Thermostat
// For control relay based on temperature
// -2 relay control
// -mode heating, cooling
// -correction for set correct actual temperature
// -delta for start again
// -statistics with min max temperature
// -menu for set settings
// -screen for display temp, stats, settings
//
// Copyright (c) 2021, Alexandre <contact@avdeveloppement.eu>.  All rights reserved.
// Copyrights licensed under the Creative Commons Attribution-ShareAlike 4.0 International Public License
// See the accompanying LICENSE file for terms.
//__________________________________________________________________________________

/**
   PIN Arduino NANO with OLED 128X64
   A4                    SDA
   A5                    SCK
   GND                   GND
   3.3V                  VDD

   PIN Arduino NANO with NTC Thermistor 10K 1% 3950 Temperature Sensor Probe Waterproof
   GND                   Thermistor PIN 1 (Both PIN are same)
   3.3V to 10k resistance to Thermistor PIN 2
                           |_ to NANO A2 and A3
   3.3V to NANO AREF (for NANO know we use 3.3V as reference)

   PIN Arduino NANO with Relay Shield
   D5                    IN1
   D6                    IN2
   GND                   DC-
   5V                    DC+

   PIN Arduino NANO with Button shield
   5V to resistor 10k to resistor 1k to button 1 to gnd
                       |              |_ to resistor 220ohms to button 2 to gnd
                       |_ Arduino NANO A6                     |_ to resistor 220ohms to button 3 to gnd
*/

#include <Arduino.h>
#include <avr/wdt.h>
// Settings save/load
#include <EEPROM.h>
// OLED Screen
#include <lcdgfx.h>
#include <lcdgfx_gui.h>
#include "menu.h"

void setup() {
  configInit();
}

void loop() {
  menuIsCanCheckAndRefresh(); // verify timer if we allow for temperature and relay check

  temperatureCheck(); // try get temperature

  relayCheck(); // if temperature changed set state relay

  menuCheck();

  //Serial.println(configFreeRam());

  configLoopDelay();
}
